# Fritzing sketch Connections (saved by Fritzing 0.9.3b)
circuit board: 4.80971cm x 5.07963cm
breadboards: 1

parts:
  U1 = NodeMCU V1.0
  J1 = female pin header, 2 pins [form="♀ (female)"]
  J2 = female pin header, 2 pins [form="♀ (female)"]
  J3 = female pin header, 2 pins [form="♀ (female)"]
  J4 = Power Jack [package=power_jack_pth_lock]
  8_Channel_Relay1 = 8 Channel Power Relay

nets (from the breadboard view):
  N1: U1.D0, J3.pin2, 8_Channel_Relay1.IN1
  N2: U1.D1, J2.pin1, 8_Channel_Relay1.IN2
  N3: U1.D2, J2.pin2, 8_Channel_Relay1.IN3
  N4: U1.D3, J1.pin1, 8_Channel_Relay1.IN4
  GND: U1.GND, J3.pin1, J4.GND, 8_Channel_Relay1.GND
  VIN: U1.Vin, J1.pin2, J4.PWR, 8_Channel_Relay1.VCC

custom parts:
  NodeMCU V1.0: ESP8266 based NodeMCU
  8 Channel Power Relay: An 8 channel power relay. The module operates at 5V.
